# Fritzing sketch Buzzer_active(module) (saved by Fritzing 0.9.3b)
breadboards: 1

parts:
  Mod1 = KY-012 Active Buzzer Module [package="Breakout board"]
  Part1 = Arduino Uno (Rev3)

nets:
  N1: Mod1.S, Part1.D8
  N2: Mod1.NC, Part1.5V
  N3: Mod1.-, Part1.GND

custom parts:
  KY-012 Active Buzzer Module: Active Piezoelectric Buzzer Module KY-012, it produces single-tone sound when signal is high. (Special thanks to vanepp for fixing the PCB holes and other errors)
